// Digital circuit A-B.dig as structural Verilog
module A_B (
  input  B2,
  input  B1,
  input  B0,
  input  A2,
  input  A1,
  input  A0,
  output R0,
  output R1,
  output R2,
  output OV_E
);

  wire add_1_c_o, add_2_c_o, decoder_1_out_0, decoder_1_out_1, decoder_1_out_2, decoder_1_out_3,
       decoder_1_out_4, decoder_1_out_5, decoder_1_out_6, decoder_1_out_7, decoder_2_out_0, decoder_2_out_1,
       decoder_2_out_2, decoder_2_out_3, decoder_2_out_4, decoder_2_out_5, decoder_2_out_6, decoder_2_out_7,
       or_2_out, or_3_out, or_4_out;
  wire [1:1] or_1_out;

  Decoder #(.Selector_Bits(3)) decoder_1 (
    .sel({B2, B1, B0}), .out_0(decoder_1_out_0), .out_1(decoder_1_out_1), .out_2(decoder_1_out_2),
    .out_3(decoder_1_out_3), .out_4(decoder_1_out_4), .out_5(decoder_1_out_5), .out_6(decoder_1_out_6),
    .out_7(decoder_1_out_7));
  or or_1 (or_1_out[1], decoder_1_out_3, decoder_1_out_2, decoder_1_out_1);
  or or_2 (or_2_out, decoder_1_out_6, decoder_1_out_5, decoder_1_out_2, decoder_1_out_1);
  or or_3 (or_3_out, decoder_1_out_7, decoder_1_out_5, decoder_1_out_3, decoder_1_out_1);
  Decoder #(.Selector_Bits(3)) decoder_2 (
    .sel({A2, or_1_out[1], R2}), .out_0(decoder_2_out_0), .out_1(decoder_2_out_1), .out_2(decoder_2_out_2),
    .out_3(decoder_2_out_3), .out_4(decoder_2_out_4), .out_5(decoder_2_out_5), .out_6(decoder_2_out_6),
    .out_7(decoder_2_out_7));
  Add add_1 (.a(A0), .b(or_3_out), .c_i(1'b0), .s(R0), .c_o(add_1_c_o));
  Add add_2 (.a(A1), .b(or_2_out), .c_i(add_1_c_o), .s(R1), .c_o(add_2_c_o));
  Add add_3 (.a(A2), .b(or_1_out[1]), .c_i(add_2_c_o), .s(R2));  // open: c_o
  or or_4 (or_4_out, decoder_2_out_6, decoder_2_out_1);
  or or_5 (OV_E, decoder_1_out_4, or_4_out);
endmodule
