// Digital circuit Comparador.dig as structural Verilog
module Comparador (
  input  A2,
  input  A1,
  input  A0,
  input  B2,
  input  B1,
  input  B0,
  output R0,
  output R1,
  output R2,
  output E
);

  Comparator #(.Signed("true"), .Bits(3)) comparator_1 (.a({A2, A1, A0}), .b({B2, B1, B0}), .gt(R0), .eq(R1), .lt(R2));

  assign E = 1'b0;
endmodule
