// Digital circuit De SM a C2.dig as structural Verilog
module De_SM_a_C2 (
  input  A2,
  input  A1,
  input  A0,
  output R2,
  output R1,
  output R0,
  output E
);

  wire decoder_1_out_0, decoder_1_out_1, decoder_1_out_2, decoder_1_out_3, decoder_1_out_5, decoder_1_out_6,
       decoder_1_out_7;

  Decoder #(.Selector_Bits(3)) decoder_1 (
    .sel({A2, A1, A0}), .out_0(decoder_1_out_0), .out_1(decoder_1_out_1), .out_2(decoder_1_out_2),
    .out_3(decoder_1_out_3), .out_4(E), .out_5(decoder_1_out_5), .out_6(decoder_1_out_6),
    .out_7(decoder_1_out_7));
  or or_1 (R2, decoder_1_out_7, decoder_1_out_6, decoder_1_out_5);
  or or_2 (R1, decoder_1_out_6, decoder_1_out_5, decoder_1_out_3, decoder_1_out_2);
  or or_3 (R0, decoder_1_out_7, decoder_1_out_5, decoder_1_out_3, decoder_1_out_1);
endmodule
