// Digital circuit solucio.dig as structural Verilog
module solucio (
  input  C0,
  input  C1,
  input  C2,
  input  A0,
  input  A1,
  input  A2,
  input  B0,
  input  B1,
  input  B2,
  output R0,
  output E,
  output R1,
  output R2
);

  wire a_b_1_ov_e, a_b_1_r0, a_b_1_r1, a_b_1_r2, comparador_1_e, comparador_1_r0, comparador_1_r1,
       comparador_1_r2, de_c2_a_sm_1_e, de_c2_a_sm_1_r0, de_c2_a_sm_1_r1, de_c2_a_sm_1_r2, de_sm_a_c2_1_e,
       de_sm_a_c2_1_r0, de_sm_a_c2_1_r1, de_sm_a_c2_1_r2, multiplicar_2_1_e, multiplicar_2_1_r0,
       multiplicar_2_1_r1, multiplicar_2_1_r2, nombres_primers_1_e, nombres_primers_1_r0,
       nombres_primers_1_r1, nombres_primers_1_r2;

  De_SM_a_C2 de_sm_a_c2_1 (
    .A2(A2), .A1(A1), .A0(A0), .R2(de_sm_a_c2_1_r2), .R1(de_sm_a_c2_1_r1), .R0(de_sm_a_c2_1_r0),
    .E(de_sm_a_c2_1_e));
  De_C2_a_SM de_c2_a_sm_1 (
    .A2(A2), .A1(A1), .A0(A0), .R2(de_c2_a_sm_1_r2), .R1(de_c2_a_sm_1_r1), .R0(de_c2_a_sm_1_r0),
    .E(de_c2_a_sm_1_e));
  A_B a_b_1 (
    .B2(B2), .B1(B1), .B0(B0), .A2(A2), .A1(A1), .A0(A0), .R0(a_b_1_r0), .R1(a_b_1_r1), .R2(a_b_1_r2),
    .OV_E(a_b_1_ov_e));
  Comparador comparador_1 (
    .A2(A2), .A1(A1), .A0(A0), .B2(B2), .B1(B1), .B0(B0), .R0(comparador_1_r0), .R1(comparador_1_r1),
    .R2(comparador_1_r2), .E(comparador_1_e));
  Multiplicar_2 multiplicar_2_1 (
    .A0(A0), .A1(A1), .A2(A2), .E(multiplicar_2_1_e), .R0(multiplicar_2_1_r0), .R1(multiplicar_2_1_r1),
    .R2(multiplicar_2_1_r2));
  Nombres_Primers nombres_primers_1 (
    .A2(A2), .A1(A1), .A0(A0), .R2(nombres_primers_1_r2), .R1(nombres_primers_1_r1),
    .R0(nombres_primers_1_r0), .E(nombres_primers_1_e));
  Multiplexer #(.Selector_Bits(3)) multiplexer_1 (
    .sel({C2, C1, C0}), .in_0(de_sm_a_c2_1_r0), .in_1(de_c2_a_sm_1_r0), .in_2(a_b_1_r0),
    .in_3(comparador_1_r0), .in_4(multiplicar_2_1_r0), .in_5(nombres_primers_1_r0), .in_6(1'b0), .in_7(1'b0),
    .out(R0));
  Multiplexer #(.Selector_Bits(3)) multiplexer_2 (
    .sel({C2, C1, C0}), .in_0(de_sm_a_c2_1_r1), .in_1(de_c2_a_sm_1_r1), .in_2(a_b_1_r1),
    .in_3(comparador_1_r1), .in_4(multiplicar_2_1_r1), .in_5(nombres_primers_1_r1), .in_6(1'b0), .in_7(1'b0),
    .out(R1));
  Multiplexer #(.Selector_Bits(3)) multiplexer_3 (
    .sel({C2, C1, C0}), .in_0(de_sm_a_c2_1_r2), .in_1(de_c2_a_sm_1_r2), .in_2(a_b_1_r2),
    .in_3(comparador_1_r2), .in_4(multiplicar_2_1_r2), .in_5(nombres_primers_1_r2), .in_6(1'b0), .in_7(1'b0),
    .out(R2));
  Multiplexer #(.Selector_Bits(3)) multiplexer_4 (
    .sel({C2, C1, C0}), .in_0(de_sm_a_c2_1_e), .in_1(de_c2_a_sm_1_e), .in_2(a_b_1_ov_e),
    .in_3(comparador_1_e), .in_4(multiplicar_2_1_e), .in_5(nombres_primers_1_e), .in_6(1'b0), .in_7(1'b0),
    .out(E));
endmodule
